# Fritzing sketch Layout (saved by Fritzing 0.9.4)
breadboards: 1

parts:
  Bauteil1 = Arduino Uno (Rev3)
  LED1 = LED - 5mm [color="Red (633nm)" package="5 mm [THT]"]
  LED2 = LED - 5mm [color="Yellow (595nm)" package="5 mm [THT]"]
  LED3 = LED - 5mm [color="Green (570nm)" package="5 mm [THT]"]
  LCD1 = LCD screen
  S1 = Pushbutton [package="[THT]"]
  S2 = Pushbutton [package="[THT]"]
  S3 = Pushbutton [package="[THT]"]
  R1 = Resistor [tolerance=±5% resistance=330 package=THT]
  R2 = Resistor [tolerance=±5% resistance=330 package=THT]
  R3 = Resistor [tolerance=±5% resistance=330 package=THT]
  R4 = Resistor [tolerance=±5% resistance=2.0k package=THT]
  R5 = Resistor [tolerance=±5% resistance=2.0k package=THT]
  R6 = Resistor [tolerance=±5% resistance=2.0k package=THT]

nets:
  N1: Bauteil1.D8, R3.Pin_0
  N2: Bauteil1.D9_PWM, R2.Pin_0
  N3: Bauteil1.D10_PWM/SS, R1.Pin_0
  N4: Bauteil1.D11_PWM/MOSI, LCD1.E
  N5: Bauteil1.D12/MISO, LCD1.RS
  N6: Bauteil1.GND, LED1.anode, LED2.anode, LED3.anode, LCD1.R/W, LCD1.LED-, S1.Pin_3, S1.Pin_4, S2.Pin_3, S2.Pin_4, S3.Pin_3, S3.Pin_4
  N7: Bauteil1.D2, LCD1.DB7
  N8: Bauteil1.D3_PWM, LCD1.DB6
  N9: Bauteil1.D4, LCD1.DB5
  N10: Bauteil1.D5_PWM, LCD1.DB4
  N11: Bauteil1.D7, S3.Pin_1, S3.Pin_2, R4.Pin_0
  5V: Bauteil1.5V, LCD1.VDD, LCD1.LED+, R4.Pin_1, R5.Pin_1, R6.Pin_1
  N12: LED1.cathode, R1.Pin_1
  N13: LED2.cathode, R2.Pin_1
  N14: LED3.cathode, R3.Pin_1
  N15: S1.Pin_1, S1.Pin_2, R6.Pin_0
  N16: S2.Pin_1, S2.Pin_2, R5.Pin_0

notes:
  PIN V0, derzeit noch über Poti; richtigen Widerstand festlegen und zwischen LCD und Versorgungsspannung hinzufügen
